// Logisim project Processor.circ as structural Verilog: 17 circuits, main circuit Processor
module Processor (
  input  Reset,
  input  [3:0] Display_Address
);

  wire alu_1_is, alu_1_is_2, bTaken, Clock, control_unit_1_isimmediate, control_unit_1_isret,
       flags_1_flags_e, flags_1_flags_gt, forwarding_unit_1_m1, forwarding_unit_1_m2, forwarding_unit_1_m6,
       forwarding_unit_1_out_9, isSt, multiplexer_15_out, not_1_out, not_2_out, not_3_out, or_1_out,
       or_2_out, or_3_out, register_14_q, register_16_q, register_17_q, register_21_q, STALL;
  wire [1:0] forwarding_unit_1_m3_rw, forwarding_unit_1_m4_ma;
  wire [2:0] control_unit_1_isubranch, multiplexer_18_out;
  wire [3:0] control_unit_1_iscall, multiplexer_9_out, multiplexer_12_out, multiplexer_17_out,
       multiplexer_19_out, register_18_q, register_22_q, register_23_q, register_24_q_2,
       register_file_1_displayd, register_file_1_displayd_2, register_file_1_displayd_4,
       register_file_1_displayd_5, register_file_1_displayd_6, register_file_1_displayd_7,
       register_file_1_displayd_8;
  wire [11:8] register_file_1_displayd_3;
  wire [12:0] control_unit_1_alusignals, multiplexer_16_out, register_15_q;
  wire [26:0] register_10_q;
  wire [31:0] adder_1_out, adder_2_out, adder_3_out, alu_1_aluresult, bit_extender_1_out,
       calculate_immediate_1_immx, memory_unit_1_ldresult, multiplexer_1_out, multiplexer_2_out,
       multiplexer_3_out, multiplexer_4_out, multiplexer_5_out, multiplexer_6_out, multiplexer_7_out,
       multiplexer_8_out, multiplexer_10_out, multiplexer_11_out, multiplexer_13_out, multiplexer_14_out,
       multiplexer_20_out, PC_q, register_1_q, register_2_q, register_3_q, register_4_q, register_5_q,
       register_6_q, register_7_q, register_8_q, register_9_q, register_11_q, register_12_q, register_13_q,
       register_19_q, register_20_q, register_24_q, register_file_1_readd1, register_file_1_readd2,
       rom_1_data, shifter_1_out;
  wire [31:27] register_10_q_2;

  Multiplexer #(.width(32), .enable("false")) multiplexer_1 (
    .in0(multiplexer_3_out), .in1(register_4_q), .out(multiplexer_1_out), .sel(isSt));
  not not_1 (not_1_out, STALL);
  Register #(.width(32), .trigger("falling")) register_1 (
    .D(register_3_q), .Q(register_1_q), .clk(Clock), .clr(Reset));  // open: en
  Register #(.width(32), .trigger("falling")) PC (
    .D(multiplexer_2_out), .en(not_2_out), .Q(PC_q), .clk(Clock), .clr(Reset));
  not not_2 (not_2_out, STALL);
  Register #(.width(32), .trigger("falling")) register_2 (
    .D(PC_q), .en(not_1_out), .Q(register_2_q), .clk(Clock), .clr(Reset));
  Register #(.width(32), .trigger("falling")) register_3 (
    .D(register_2_q), .Q(register_3_q), .clk(Clock), .clr(Reset));  // open: en
  Register #(.width(32), .trigger("falling")) register_4 (
    .D(multiplexer_7_out), .Q(register_4_q), .clk(Clock), .clr(Reset));  // open: en
  Register #(.width(32), .trigger("falling")) register_5 (
    .D(register_1_q), .Q(register_5_q), .clk(Clock), .clr(Reset));  // open: en
  Multiplexer #(.width(32), .enable("false")) multiplexer_2 (
    .in0(adder_1_out), .in1(multiplexer_5_out), .out(multiplexer_2_out), .sel(bTaken));
  assign bit_extender_1_out = {{5{register_10_q[26]}}, register_10_q};  // Bit_Extender bit_extender_1
  Multiplexer #(.select(2), .width(32), .enable("false")) multiplexer_3 (
    .in0(register_4_q), .in1(multiplexer_6_out), .in2(register_8_q), .in3(register_8_q),
    .out(multiplexer_3_out), .sel(forwarding_unit_1_m4_ma));
  Register #(.width(32), .trigger("falling")) register_6 (
    .D(register_8_q), .Q(register_6_q), .clk(Clock), .clr(Reset));  // open: en
  Adder #(.width(32)) adder_1 (.a(32'h4), .b(PC_q), .out(adder_1_out));  // open: cin, cout
  Shifter #(.width(32)) shifter_1 (.in(bit_extender_1_out), .\dist (5'b00010), .out(shifter_1_out));
  Multiplexer #(.select(2), .width(32), .enable("false")) multiplexer_4 (
    .in0(register_11_q), .in1(multiplexer_6_out), .in2(register_8_q), .in3(register_8_q),
    .out(multiplexer_4_out), .sel(forwarding_unit_1_m3_rw));
  ALU alu_1 (
    .A(multiplexer_4_out), .B(multiplexer_1_out), .ALUsignals(register_15_q), .aluResult(alu_1_aluresult),
    .is(alu_1_is), .is_2(alu_1_is_2));
  Adder #(.width(32)) adder_2 (.a(register_5_q), .b(32'h4), .out(adder_2_out));  // open: cin, cout
  Calculate_Immediate calculate_immediate_1 (.imm(register_10_q[17:0]), .immx(calculate_immediate_1_immx));
  Adder #(.width(32)) adder_3 (.a(shifter_1_out), .b(register_2_q), .out(adder_3_out));  // open: cin, cout
  Register #(.width(32), .trigger("falling")) register_7 (
    .D(adder_3_out), .Q(register_7_q), .clk(Clock), .clr(Reset));  // open: en
  Multiplexer #(.width(32), .enable("false")) multiplexer_5 (
    .in0(register_7_q), .in1(multiplexer_4_out), .out(multiplexer_5_out), .sel(register_14_q));
  Register #(.width(32), .trigger("falling")) register_8 (
    .D(alu_1_aluresult), .Q(register_8_q), .clk(Clock), .clr(Reset));  // open: en
  Register #(.width(32), .trigger("falling")) register_9 (
    .D(memory_unit_1_ldresult), .Q(register_9_q), .clk(Clock), .clr(Reset));  // open: en
  Multiplexer #(.select(2), .width(32), .enable("false")) multiplexer_6 (
    .in0(register_6_q), .in1(register_9_q), .in2(adder_2_out), .out(multiplexer_6_out),
    .sel({register_23_q[0], register_23_q[2]}));  // open: in3
  Clock u_Clock (.out(Clock));
  ROM #(.addrWidth(24), .dataWidth(32)) rom_1 (.addr(PC_q[25:2]), .data(rom_1_data));  // open: sel
  Multiplexer #(.width(32), .enable("false")) multiplexer_7 (
    .in0(multiplexer_10_out), .in1(calculate_immediate_1_immx), .out(multiplexer_7_out),
    .sel(control_unit_1_isimmediate));
  Flags flags_1 (
    .isCmp(register_15_q[0]), .is(alu_1_is), .is_2(alu_1_is_2), .flags_GT(flags_1_flags_gt),
    .flags_E(flags_1_flags_e));
  Memory_Unit memory_unit_1 (
    .MAR(register_8_q), .ldResult(memory_unit_1_ldresult), .MDR(multiplexer_11_out), .isSt(register_22_q[1]),
    .isLd(register_22_q[2]), .Clock(Clock), .Reset(Reset));
  Hex_Digit_Display hex_digit_display_1 (.value(register_file_1_displayd_8));  // open: dp
  Multiplexer #(.width(32), .enable("false")) multiplexer_8 (
    .in0(rom_1_data), .in1(32'h68000000), .out(multiplexer_8_out), .sel(bTaken));
  Register #(.width(32), .trigger("falling")) register_10 (
    .D(multiplexer_8_out), .en(not_3_out), .Q({register_10_q_2, register_10_q}), .clk(Clock), .clr(Reset));
  not not_3 (not_3_out, STALL);
  Multiplexer #(.width(4), .enable("false")) multiplexer_9 (
    .in0(register_10_q[17:14]), .in1(register_10_q[25:22]), .out(multiplexer_9_out),
    .sel(control_unit_1_iscall[1]));
  Multiplexer #(.width(32), .enable("false")) multiplexer_10 (
    .in0(register_file_1_readd2), .in1(multiplexer_6_out), .out(multiplexer_10_out),
    .sel(forwarding_unit_1_m2));
  Register #(.width(32), .trigger("falling")) register_11 (
    .D(multiplexer_13_out), .Q(register_11_q), .clk(Clock), .clr(Reset));  // open: en
  Register #(.width(32), .trigger("falling")) register_12 (
    .D(multiplexer_10_out), .Q(register_12_q), .clk(Clock), .clr(Reset));  // open: en
  Multiplexer #(.width(32), .enable("false")) multiplexer_11 (
    .in0(register_13_q), .in1(multiplexer_6_out), .out(multiplexer_11_out), .sel(forwarding_unit_1_m6));
  Forwarding_Unit forwarding_unit_1 (
    .in_1({register_10_q_2, register_10_q}), .in_2(register_19_q), .in_3(register_20_q),
    .in_4({register_24_q[31:26], register_24_q_2, register_24_q[21:0]}), .M1(forwarding_unit_1_m1),
    .M2(forwarding_unit_1_m2), .M3_rw(forwarding_unit_1_m3_rw), .M4_ma(forwarding_unit_1_m4_ma),
    .out_9(forwarding_unit_1_out_9), .M6(forwarding_unit_1_m6));
  Hex_Digit_Display hex_digit_display_2 (.value(register_file_1_displayd_7));  // open: dp
  Multiplexer #(.width(4), .enable("false")) multiplexer_12 (
    .in0(register_10_q[21:18]), .in1(4'b1111), .out(multiplexer_12_out), .sel(control_unit_1_isret));
  Register_File register_file_1 (
    .ReadA1(multiplexer_12_out), .ReadA2(multiplexer_9_out), .WriteE(register_23_q[3]),
    .WriteD(multiplexer_6_out), .ReadD1(register_file_1_readd1), .ReadD2(register_file_1_readd2),
    .Clock(Clock), .Reset(Reset),
    .DisplayD({register_file_1_displayd_8, register_file_1_displayd_7, register_file_1_displayd_6, register_file_1_displayd_5, register_file_1_displayd_4, register_file_1_displayd_3, register_file_1_displayd_2, register_file_1_displayd}),
    .DisplayA(Display_Address), .WriteA(multiplexer_17_out));
  Multiplexer #(.width(32), .enable("false")) multiplexer_13 (
    .in0(register_file_1_readd1), .in1(multiplexer_6_out), .out(multiplexer_13_out),
    .sel(forwarding_unit_1_m1));
  Register #(.width(32), .trigger("falling")) register_13 (
    .D(multiplexer_14_out), .Q(register_13_q), .clk(Clock), .clr(Reset));  // open: en
  Multiplexer #(.width(32), .enable("false")) multiplexer_14 (
    .in0(register_12_q), .in1(multiplexer_6_out), .out(multiplexer_14_out), .sel(forwarding_unit_1_out_9));
  Hex_Digit_Display hex_digit_display_3 (.value(register_file_1_displayd_6));  // open: dp
  Multiplexer #(.enable("false")) multiplexer_15 (
    .in0(control_unit_1_isret), .in1(1'b0), .out(multiplexer_15_out), .sel(or_2_out));
  Multiplexer #(.width(13), .enable("false")) multiplexer_16 (
    .in0(control_unit_1_alusignals), .in1({13{1'b0}}), .out(multiplexer_16_out), .sel(or_1_out));
  Branch_Unit branch_unit_1 (
    .isBeq(register_21_q), .isUBranch(register_17_q), .flags_E(flags_1_flags_e), .isBgt(register_16_q),
    .flags_GT(flags_1_flags_gt), .isBranchTaken(bTaken));
  or or_1 (or_1_out, bTaken, STALL);
  Hex_Digit_Display hex_digit_display_4 (.value(register_file_1_displayd_5));  // open: dp
  Hex_Digit_Display hex_digit_display_5 (.value(register_file_1_displayd_4));  // open: dp
  Control_Unit control_unit_1 (
    .isSt(control_unit_1_iscall[1]), .isLd(control_unit_1_iscall[2]), .isBeq(control_unit_1_isubranch[2]),
    .isBgt(control_unit_1_isubranch[1]), .isRet(control_unit_1_isret), .I_bit(register_10_q[26]),
    .isImmediate(control_unit_1_isimmediate), .opcode(register_10_q_2), .isWb(control_unit_1_iscall[3]),
    .isUbranch(control_unit_1_isubranch[0]), .isCall(control_unit_1_iscall[0]),
    .ALUsignals(control_unit_1_alusignals));
  Register #(.width(1), .trigger("falling")) register_14 (
    .D(multiplexer_15_out), .Q(register_14_q), .clk(Clock), .clr(Reset));  // open: en
  Register #(.width(13), .trigger("falling")) register_15 (
    .D(multiplexer_16_out), .Q(register_15_q), .clk(Clock), .clr(Reset));  // open: en
  Hex_Digit_Display hex_digit_display_6 (.value(register_file_1_displayd_3));  // open: dp
  Hex_Digit_Display hex_digit_display_7 (.value(register_file_1_displayd_2));  // open: dp
  Multiplexer #(.width(4), .enable("false")) multiplexer_17 (
    .in0(register_24_q_2), .in1(4'b1111), .out(multiplexer_17_out), .sel(register_23_q[0]));
  Hex_Digit_Display hex_digit_display_8 (.value(register_file_1_displayd));  // open: dp
  Multiplexer #(.width(3), .enable("false")) multiplexer_18 (
    .in0(control_unit_1_isubranch), .in1(3'b000), .out(multiplexer_18_out), .sel(or_2_out));
  Multiplexer #(.width(4), .enable("false")) multiplexer_19 (
    .in0(control_unit_1_iscall), .in1(4'b0000), .out(multiplexer_19_out), .sel(or_2_out));
  Multiplexer #(.width(32), .enable("false")) multiplexer_20 (
    .in0({register_10_q_2, register_10_q}), .in1(32'h68000000), .out(multiplexer_20_out), .sel(or_3_out));
  Register #(.width(1), .trigger("falling")) register_16 (
    .D(multiplexer_18_out[1]), .Q(register_16_q), .clk(Clock), .clr(Reset));  // open: en
  Register #(.width(1), .trigger("falling")) register_17 (
    .D(multiplexer_18_out[0]), .Q(register_17_q), .clk(Clock), .clr(Reset));  // open: en
  or or_2 (or_2_out, STALL, bTaken);
  Register #(.width(4), .trigger("falling")) register_18 (
    .D(multiplexer_19_out), .Q({register_18_q[3:2], isSt, register_18_q[0]}), .clk(Clock), .clr(Reset));  // open: en
  Register #(.width(32), .trigger("falling")) register_19 (
    .D(multiplexer_20_out), .Q(register_19_q), .clk(Clock), .clr(Reset));  // open: en
  Register #(.width(32), .trigger("falling")) register_20 (
    .D(register_19_q), .Q(register_20_q), .clk(Clock), .clr(Reset));  // open: en
  Register #(.width(1), .trigger("falling")) register_21 (
    .D(multiplexer_18_out[2]), .Q(register_21_q), .clk(Clock), .clr(Reset));  // open: en
  Register #(.width(4), .trigger("falling")) register_22 (
    .D({register_18_q[3:2], isSt, register_18_q[0]}), .Q(register_22_q), .clk(Clock), .clr(Reset));  // open: en
  Register #(.width(4), .trigger("falling")) register_23 (
    .D(register_22_q), .Q(register_23_q), .clk(Clock), .clr(Reset));  // open: en
  Register #(.width(32), .trigger("falling")) register_24 (
    .D(register_20_q), .Q({register_24_q[31:26], register_24_q_2, register_24_q[21:0]}), .clk(Clock),
    .clr(Reset));  // open: en
  or or_3 (or_3_out, bTaken, STALL);
  Data_lock_Unit data_lock_unit_1 (.in_1({register_10_q_2, register_10_q}), .in_2(register_19_q), .out_3(STALL));

  // Notes on the sheet:
  //   OF-EX B
  //   EX-MA
  //   PC
  //   IF-OF PC
  //   OF_EX PC
  //   MA-RW
  //   isBranchTaken
  //   M4
  //   ALUsignals
  //   MA-RW aluRes
  //   pc
  //   pc+4
  //   branchTarget
  //   offset
  //   pc
  //   M3
  //   B
  //   ALU
  //   aluResult
  //   EX-MA
  //   MAR
  //   Instruction Memory
  //   calc immx
  //   imm
  //   OF-EX
  //   isBranchTaken
  //   A
  //   is>
  //   is=
  //   MDR
  //   Memory
  //   Unit
  //   MA-RW
  //   data
  //   SINGLE CYCLE PROCESSOR
  //   contents of rom_1 (hex, n*v repeats v):
  //   4c000000 4c40000c 7c400000 4c400007 7c400004 4c40000b 7c400008 4c400009 7c40000c 4c400003 7c400010
  //   4c40000f 7c400014 4c800000 4cc00006 98000002 90000000 4900c000 75480000 75880004 28158000 88000002
  //   90000003 7d880000 7d480004 4880004 d100001 2c100001 8ffffff6 48800000 ccc0001 4900c000 2c0c0001
  //   8ffffff1 a0000000
  //   Btarget
  //   immx
  //   isRet
  //   Flags
  //   isCmp
  //   isLd
  //   M6
  //   isSt
  //   ldResult
  //   isLd
  //   isCall
  //   instruction IF_OF
  //   rd
  //   isSt
  //   op2
  //   isImmediate
  //   OF-EX A
  //   flags(GT)
  //   flags(E)
  //   OF-EX OP2
  //   rs1
  //   E
  //   Register
  //   A
  //   File
  //   D
  //   op1
  //   M2   M1
  //   Branch
  //   Unit
  //   EX-MA OP2
  //   M5
  //   isRet
  //   isWb
  //   address
  //   data
  //   isBeq
  //   isBgt
  //   isUBranch
  //   Display Register
  //   opcode
  //   CONTROL
  //   I bit
  //   UNIT
  //   OF-EX isRet
  //   OF-EX ALU
  //   isCall
  //   rd
  //   OF-EX
  //   EX-MA
  //   MA-RW
  //   OF-EX
  //   Branch
  //   Instruction
  //   OF-EX-MA-RW
endmodule

module Control_Unit (
  input  I_bit,
  input  [4:0] opcode,
  output isSt,
  output isLd,
  output isBeq,
  output isBgt,
  output isRet,
  output isImmediate,
  output isWb,
  output isUbranch,
  output isCall,
  output [12:0] ALUsignals
);

  wire and_6_out, and_7_out, and_8_out, and_9_out, and_10_out, and_12_out, and_13_out, nand_1_out;

  nand nand_1 (nand_1_out, opcode[0], opcode[1]);
  and and_1 (isSt, opcode[0], opcode[1], opcode[2], opcode[3], ~opcode[4]);  // AND_Gate
  and and_2 (isLd, ~opcode[0], opcode[1], opcode[2], opcode[3], ~opcode[4]);  // AND_Gate
  and and_3 (isBeq, ~opcode[0], ~opcode[1], ~opcode[2], ~opcode[3], opcode[4]);  // AND_Gate
  and and_4 (isBgt, opcode[0], ~opcode[1], ~opcode[2], ~opcode[3], opcode[4]);  // AND_Gate
  and and_5 (isRet, ~opcode[0], ~opcode[1], opcode[2], ~opcode[3], opcode[4]);  // AND_Gate
  and and_6 (and_6_out, opcode[0], ~opcode[1], opcode[2], ~opcode[4]);  // AND_Gate
  and and_7 (and_7_out, opcode[0], opcode[2], opcode[3], ~opcode[4]);  // AND_Gate
  and and_8 (and_8_out, opcode[4], nand_1_out);
  and and_9 (and_9_out, opcode[1], ~opcode[2], ~opcode[3], opcode[4]);  // AND_Gate
  and and_10 (and_10_out, ~opcode[0], ~opcode[1], opcode[2], ~opcode[3], opcode[4]);  // AND_Gate
  and and_11 (isCall, opcode[0], opcode[1], ~opcode[2], ~opcode[3], opcode[4]);  // AND_Gate
  and and_12 (and_12_out, ~opcode[0], ~opcode[1], ~opcode[2], ~opcode[3], ~opcode[4]);  // AND_Gate
  and and_13 (and_13_out, opcode[1], opcode[2], opcode[3], ~opcode[4]);  // AND_Gate
  and isSub (ALUsignals[2], opcode[0], ~opcode[1], ~opcode[2], ~opcode[3], ~opcode[4]);  // AND_Gate
  and isCmp (ALUsignals[0], opcode[0], ~opcode[1], opcode[2], ~opcode[3], ~opcode[4]);  // AND_Gate
  and isMul (ALUsignals[3], ~opcode[0], opcode[1], ~opcode[2], ~opcode[3], ~opcode[4]);  // AND_Gate
  and isDiv (ALUsignals[4], opcode[0], opcode[1], ~opcode[2], ~opcode[3], ~opcode[4]);  // AND_Gate
  and isMod (ALUsignals[5], ~opcode[0], ~opcode[1], opcode[2], ~opcode[3], ~opcode[4]);  // AND_Gate
  and isLsl (ALUsignals[7], ~opcode[0], opcode[1], ~opcode[2], opcode[3], ~opcode[4]);  // AND_Gate
  and isLsr (ALUsignals[8], opcode[0], opcode[1], ~opcode[2], opcode[3], ~opcode[4]);  // AND_Gate
  and isAsr (ALUsignals[9], ~opcode[0], ~opcode[1], opcode[2], opcode[3], ~opcode[4]);  // AND_Gate
  and isOr (ALUsignals[12], opcode[0], opcode[1], opcode[2], ~opcode[3], ~opcode[4]);  // AND_Gate
  and isAnd (ALUsignals[11], ~opcode[0], opcode[1], opcode[2], ~opcode[3], ~opcode[4]);  // AND_Gate
  and isNot (ALUsignals[10], ~opcode[0], ~opcode[1], ~opcode[2], opcode[3], ~opcode[4]);  // AND_Gate
  and isMov (ALUsignals[6], opcode[0], ~opcode[1], ~opcode[2], opcode[3], ~opcode[4]);  // AND_Gate
  or or_1 (isUbranch, and_9_out, and_10_out);
  or isAdd (ALUsignals[1], and_12_out, and_13_out);
  nor nor_1 (isWb, and_6_out, and_7_out, and_8_out);

  assign isImmediate = I_bit;

  // Notes on the sheet:
  //   op1
  //   op2
  //   op3
  //   op4
  //   op5
endmodule

module Register_File (
  input  Clock,
  input  Reset,
  input  [31:0] WriteD,
  input  [3:0] ReadA1,
  input  WriteE,
  input  [3:0] WriteA,
  input  [3:0] ReadA2,
  input  [3:0] DisplayA,
  output [31:0] ReadD1,
  output [31:0] ReadD2,
  output [31:0] DisplayD
);

  wire demultiplexer_1_out0, demultiplexer_1_out1, demultiplexer_1_out2, demultiplexer_1_out3,
       demultiplexer_1_out4, demultiplexer_1_out5, demultiplexer_1_out6, demultiplexer_1_out7,
       demultiplexer_1_out8, demultiplexer_1_out9, demultiplexer_1_out10, demultiplexer_1_out11,
       demultiplexer_1_out12, demultiplexer_1_out13, demultiplexer_1_out14, demultiplexer_1_out15,
       multiplexer_2_out, or_1_out, or_2_out;
  wire [31:0] multiplexer_1_out, r0_q, r1_q, r2_q, r3_q, r4_q, r5_q, r6_q, r7_q, r8_q, r9_q, r10_q, r11_q,
       r12_q, r13_q, r14_q, r15_q;

  Demultiplexer #(.select(4), .disabled(0), .enable("false")) demultiplexer_1 (
    .out0(demultiplexer_1_out0), .out1(demultiplexer_1_out1), .out2(demultiplexer_1_out2),
    .out3(demultiplexer_1_out3), .out4(demultiplexer_1_out4), .out5(demultiplexer_1_out5),
    .out6(demultiplexer_1_out6), .out7(demultiplexer_1_out7), .out8(demultiplexer_1_out8),
    .out9(demultiplexer_1_out9), .out10(demultiplexer_1_out10), .out11(demultiplexer_1_out11),
    .out12(demultiplexer_1_out12), .out13(demultiplexer_1_out13), .out14(demultiplexer_1_out14),
    .out15(demultiplexer_1_out15), .in(WriteE), .sel(WriteA));
  Multiplexer #(.width(32), .enable("false")) multiplexer_1 (
    .in0(WriteD), .in1(32'h3fffffc), .out(multiplexer_1_out), .sel(Reset));
  or or_1 (or_1_out, demultiplexer_1_out14, Reset);
  Multiplexer #(.enable("false")) multiplexer_2 (.in0(or_2_out), .out(multiplexer_2_out), .sel(1'b0));  // open: in1
  or or_2 (or_2_out, Clock, Reset);
  Register #(.width(32)) r0 (.D(WriteD), .en(demultiplexer_1_out0), .Q(r0_q), .clk(Clock), .clr(Reset));
  Register #(.width(32)) r1 (.D(WriteD), .en(demultiplexer_1_out1), .Q(r1_q), .clk(Clock), .clr(Reset));
  Register #(.width(32)) r2 (.D(WriteD), .en(demultiplexer_1_out2), .Q(r2_q), .clk(Clock), .clr(Reset));
  Register #(.width(32)) r3 (.D(WriteD), .en(demultiplexer_1_out3), .Q(r3_q), .clk(Clock), .clr(Reset));
  Register #(.width(32)) r4 (.D(WriteD), .en(demultiplexer_1_out4), .Q(r4_q), .clk(Clock), .clr(Reset));
  Register #(.width(32)) r5 (.D(WriteD), .en(demultiplexer_1_out5), .Q(r5_q), .clk(Clock), .clr(Reset));
  Register #(.width(32)) r6 (.D(WriteD), .en(demultiplexer_1_out6), .Q(r6_q), .clk(Clock), .clr(Reset));
  Register #(.width(32)) r7 (.D(WriteD), .en(demultiplexer_1_out7), .Q(r7_q), .clk(Clock), .clr(Reset));
  Register #(.width(32)) r8 (.D(WriteD), .en(demultiplexer_1_out8), .Q(r8_q), .clk(Clock), .clr(Reset));
  Register #(.width(32)) r9 (.D(WriteD), .en(demultiplexer_1_out9), .Q(r9_q), .clk(Clock), .clr(Reset));
  Register #(.width(32)) r10 (.D(WriteD), .en(demultiplexer_1_out10), .Q(r10_q), .clk(Clock), .clr(Reset));
  Register #(.width(32)) r11 (.D(WriteD), .en(demultiplexer_1_out11), .Q(r11_q), .clk(Clock), .clr(Reset));
  Register #(.width(32)) r12 (.D(WriteD), .en(demultiplexer_1_out12), .Q(r12_q), .clk(Clock), .clr(Reset));
  Register #(.width(32)) r13 (.D(WriteD), .en(demultiplexer_1_out13), .Q(r13_q), .clk(Clock), .clr(Reset));
  Register #(.width(32)) r14 (.D(multiplexer_1_out), .en(or_1_out), .Q(r14_q), .clk(multiplexer_2_out));  // open: clr
  Register #(.width(32)) r15 (.D(WriteD), .en(demultiplexer_1_out15), .Q(r15_q), .clk(Clock), .clr(Reset));
  Multiplexer #(.select(4), .width(32), .disabled(0), .enable("false")) multiplexer_3 (
    .in0(r0_q), .in1(r1_q), .in2(r2_q), .in3(r3_q), .in4(r4_q), .in5(r5_q), .in6(r6_q), .in7(r7_q),
    .in8(r8_q), .in9(r9_q), .in10(r10_q), .in11(r11_q), .in12(r12_q), .in13(r13_q), .in14(r14_q),
    .in15(r15_q), .out(ReadD1), .sel(ReadA1));
  Multiplexer #(.select(4), .width(32), .disabled(0), .enable("false")) multiplexer_4 (
    .in0(r0_q), .in1(r1_q), .in2(r2_q), .in3(r3_q), .in4(r4_q), .in5(r5_q), .in6(r6_q), .in7(r7_q),
    .in8(r8_q), .in9(r9_q), .in10(r10_q), .in11(r11_q), .in12(r12_q), .in13(r13_q), .in14(r14_q),
    .in15(r15_q), .out(ReadD2), .sel(ReadA2));
  Multiplexer #(.select(4), .width(32), .disabled(0), .enable("false")) multiplexer_5 (
    .in0(r0_q), .in1(r1_q), .in2(r2_q), .in3(r3_q), .in4(r4_q), .in5(r5_q), .in6(r6_q), .in7(r7_q),
    .in8(r8_q), .in9(r9_q), .in10(r10_q), .in11(r11_q), .in12(r12_q), .in13(r13_q), .in14(r14_q),
    .in15(r15_q), .out(DisplayD), .sel(DisplayA));
endmodule

module ALU (
  input  [31:0] A,
  input  [31:0] B,
  input  [12:0] ALUsignals,
  output [31:0] aluResult,
  output is,
  output is_2
);

  wire [31:0] adder_1_out, and_1_out, divider_1_out, divider_1_rem, multiplier_1_out, not_1_out, or_1_out,
       shifter_1_out, shifter_2_out, shifter_3_out, subtractor_1_out;

  Adder #(.width(32)) adder_1 (.a(A), .b(B), .out(adder_1_out));  // open: cin, cout
  Subtractor #(.width(32)) subtractor_1 (.a(A), .b(B), .out(subtractor_1_out));  // open: bin, bout
  Multiplier #(.width(32)) multiplier_1 (.a(A), .b(B), .out(multiplier_1_out));  // open: cin, cout
  Divider #(.width(32)) divider_1 (.a(A), .b(B), .out(divider_1_out), .rem(divider_1_rem));  // open: upper
  Comparator #(.width(32)) comparator_1 (.a(A), .b(B), .gt(is), .eq(is_2));  // open: lt
  Shifter #(.width(32)) shifter_1 (.in(A), .\dist (B[4:0]), .out(shifter_1_out));
  Shifter #(.width(32), .shift("lr")) shifter_2 (.in(A), .\dist (B[4:0]), .out(shifter_2_out));
  Shifter #(.width(32), .shift("ar")) shifter_3 (.in(A), .\dist (B[4:0]), .out(shifter_3_out));
  assign not_1_out = ~B;  // NOT_Gate not_1, 32 bits wide
  assign and_1_out = A & B;  // AND_Gate and_1, 32 bits wide
  assign or_1_out = A | B;  // OR_Gate or_1, 32 bits wide
  assign aluResult = ALUsignals[1] ? adder_1_out : 32'bz;  // Controlled_Buffer controlled_buffer_1
  assign aluResult = ALUsignals[2] ? subtractor_1_out : 32'bz;  // Controlled_Buffer controlled_buffer_2
  assign aluResult = ALUsignals[3] ? multiplier_1_out : 32'bz;  // Controlled_Buffer controlled_buffer_3
  assign aluResult = ALUsignals[4] ? divider_1_out : 32'bz;  // Controlled_Buffer controlled_buffer_4
  assign aluResult = ALUsignals[5] ? divider_1_rem : 32'bz;  // Controlled_Buffer controlled_buffer_5
  assign aluResult = ALUsignals[6] ? B : 32'bz;  // Controlled_Buffer controlled_buffer_6
  assign aluResult = ALUsignals[7] ? shifter_1_out : 32'bz;  // Controlled_Buffer controlled_buffer_7
  assign aluResult = ALUsignals[8] ? shifter_2_out : 32'bz;  // Controlled_Buffer controlled_buffer_8
  assign aluResult = ALUsignals[9] ? shifter_3_out : 32'bz;  // Controlled_Buffer controlled_buffer_9
  assign aluResult = ALUsignals[10] ? not_1_out : 32'bz;  // Controlled_Buffer controlled_buffer_10
  assign aluResult = ALUsignals[11] ? and_1_out : 32'bz;  // Controlled_Buffer controlled_buffer_11
  assign aluResult = ALUsignals[12] ? or_1_out : 32'bz;  // Controlled_Buffer controlled_buffer_12

  // Notes on the sheet:
  //   add
  //   sub
  //   mul
  //   div
  //   cmp
  //   lsr
  //   mod
  //   lsl
  //   asr
endmodule

module Flags (
  input  isCmp,
  input  is,
  input  is_2,
  output flags_GT,
  output flags_E
);

  D_Flip_Flop #(.trigger("high")) d_ff_1 (.clk(isCmp), .D(is), .Q(flags_GT));  // open: Qn, preset, en, reset
  D_Flip_Flop #(.trigger("high")) d_ff_2 (.clk(isCmp), .D(is_2), .Q(flags_E));  // open: Qn, preset, en, reset
endmodule

module Branch_Unit (
  input  isUBranch,
  input  isBeq,
  input  flags_E,
  input  isBgt,
  input  flags_GT,
  output isBranchTaken
);

  wire and_1_out, and_2_out;

  and and_1 (and_1_out, isBeq, flags_E);
  and and_2 (and_2_out, isBgt, flags_GT);
  or or_1 (isBranchTaken, isUBranch, and_1_out, and_2_out);
endmodule

module Memory_Unit (
  input  [31:0] MAR,
  input  isLd,
  input  [31:0] MDR,
  input  isSt,
  input  Clock,
  input  Reset,
  output [31:0] ldResult
);

  RAM #(.addrWidth(24), .dataWidth(32), .bus("separate")) ram_1 (
    .addr(MAR[25:2]), .din(MDR), .data(ldResult), .str(isSt), .clk(Clock), .ld(isLd), .clr(Reset));  // open: sel
endmodule

module Calculate_Immediate (
  input  [17:0] imm,
  output [31:0] immx
);

  wire [31:0] bit_extender_1_out, bit_extender_2_out, shifter_1_out;

  assign bit_extender_1_out = {{16{1'b0}}, imm[15:0]};  // Bit_Extender bit_extender_1
  assign bit_extender_2_out = {{16{imm[15]}}, imm[15:0]};  // Bit_Extender bit_extender_2
  Shifter #(.width(32)) shifter_1 (.in(bit_extender_1_out), .\dist (5'b10000), .out(shifter_1_out));
  Multiplexer #(.select(2), .width(32), .enable("false")) multiplexer_1 (
    .in0(bit_extender_2_out), .in1(bit_extender_1_out), .in2(shifter_1_out), .out(immx), .sel(imm[17:16]));  // open: in3

  // Notes on the sheet:
  //   modifier bits
  //   high
  //   default
  //   unsigned
endmodule

module A_belongsTo (
  input  [4:0] opcode,
  output out_2
);

  wire and_1_out, and_2_out, and_3_out, and_4_out, and_5_out, not_1_out, not_2_out, not_3_out, not_4_out;

  not not_1 (not_1_out, opcode[1]);
  not not_2 (not_2_out, opcode[0]);
  not not_3 (not_3_out, opcode[1]);
  not not_4 (not_4_out, opcode[2]);
  and and_1 (and_1_out, opcode[0], not_1_out, opcode[2], opcode[3], ~opcode[4]);  // AND_Gate
  and and_2 (and_2_out, ~opcode[0], opcode[1], ~opcode[2], ~opcode[3], opcode[4]);  // AND_Gate
  and and_3 (and_3_out, ~opcode[0], ~opcode[1], ~opcode[2], ~opcode[3], opcode[4]);  // AND_Gate
  and and_4 (and_4_out, opcode[0], ~opcode[1], ~opcode[2], ~opcode[3], opcode[4]);  // AND_Gate
  and and_5 (and_5_out, ~not_2_out, ~not_3_out, not_4_out, ~opcode[3], opcode[4]);  // AND_Gate
  or or_1 (out_2, and_1_out, and_2_out, and_3_out, and_4_out, and_5_out);

  // Notes on the sheet:
  //   op1
  //   op2
  //   op3
  //   op4
  //   op5
  //   isNop
  //   Is Branch
  //   isBeq
  //   isBgt
  //   isCall
endmodule

module Data_lock_Unit (
  input  [31:0] in_1,
  input  [31:0] in_2,
  output out_3
);

  wire and_1_out, and_2_out, Branch_Ins_out_2, comparator_1_eq, comparator_2_eq, comparator_3_eq,
       comparator_4_eq, isMov_out, isNot_out, isRet_out, isSt_out, or_1_out, or_2_out, or_3_out, ret_ra_out,
       rs1_match_out, rs2_match_out, St_rd_out;

  and isSt (isSt_out, in_1[27], in_1[28], in_1[29], in_1[30], ~in_1[31]);  // AND_Gate
  and and_1 (and_1_out, ~in_2[27], in_2[28], in_2[29], in_2[30], ~in_2[31]);  // AND_Gate
  and isNot (isNot_out, ~in_1[27], ~in_1[28], ~in_1[29], in_1[30], ~in_1[31]);  // AND_Gate
  and isMov (isMov_out, in_1[27], ~in_1[28], ~in_1[29], in_1[30], ~in_1[31]);  // AND_Gate
  or or_1 (or_1_out, isNot_out, isMov_out);
  Comparator #(.width(4), .mode("unsigned")) comparator_1 (
    .a(in_2[25:22]), .b(in_1[25:22]), .eq(comparator_1_eq));  // open: gt, lt
  Comparator #(.width(4), .mode("unsigned")) comparator_2 (
    .a(in_2[25:22]), .b(in_1[21:18]), .eq(comparator_2_eq));  // open: gt, lt
  Comparator #(.width(4), .mode("unsigned")) comparator_3 (
    .a(in_2[25:22]), .b(in_1[17:14]), .eq(comparator_3_eq));  // open: gt, lt
  Comparator #(.width(4), .mode("unsigned")) comparator_4 (
    .a(4'b1111), .b(in_2[25:22]), .eq(comparator_4_eq));  // open: gt, lt
  and isRet (isRet_out, ~in_1[27], ~in_1[28], in_1[29], ~in_1[30], in_1[31]);  // AND_Gate
  A_belongsTo Branch_Ins (.opcode(in_1[31:27]), .out_2(Branch_Ins_out_2));
  and St_rd (St_rd_out, isSt_out, comparator_1_eq);
  and rs1_match (rs1_match_out, ~or_1_out, comparator_2_eq);  // AND_Gate
  and rs2_match (rs2_match_out, ~in_1[26], ~or_2_out, comparator_3_eq);  // AND_Gate
  and ret_ra (ret_ra_out, isRet_out, comparator_4_eq);
  and and_2 (and_2_out, ~in_1[27], in_1[28], in_1[29], in_1[30], ~in_1[31]);  // AND_Gate
  or or_2 (or_2_out, and_2_out, isSt_out);
  or or_3 (or_3_out, St_rd_out, rs1_match_out, rs2_match_out, ret_ra_out);
  and and_3 (out_3, ~Branch_Ins_out_2, or_3_out, and_1_out);  // AND_Gate

  // Notes on the sheet:
  //   IF-OF
  //   OF-EX
  //   instructions
  //   I
  //   rd
  //   rs1
  //   rs2
  //   isLd
  //   rd
  //   isLd
endmodule

module _6_A_belongsTo (
  input  [4:0] opcode,
  output out_2
);

  wire and_1_out, and_2_out, and_3_out, and_4_out, and_5_out, and_6_out, and_7_out;

  and and_1 (and_1_out, opcode[0], opcode[1], ~opcode[2], ~opcode[3], opcode[4]);  // AND_Gate
  and and_2 (and_2_out, ~opcode[0], opcode[1], ~opcode[2], ~opcode[3], opcode[4]);  // AND_Gate
  and and_3 (and_3_out, ~opcode[0], ~opcode[1], ~opcode[2], ~opcode[3], opcode[4]);  // AND_Gate
  and and_4 (and_4_out, opcode[0], ~opcode[1], ~opcode[2], ~opcode[3], opcode[4]);  // AND_Gate
  and and_5 (and_5_out, ~opcode[0], ~opcode[1], ~opcode[2], opcode[3], ~opcode[4]);  // AND_Gate
  and and_6 (and_6_out, opcode[0], ~opcode[1], ~opcode[2], opcode[3], ~opcode[4]);  // AND_Gate
  and and_7 (and_7_out, opcode[0], ~opcode[1], opcode[3], ~opcode[4]);  // AND_Gate
  or or_1 (out_2, and_1_out, and_2_out, and_3_out, and_4_out, and_5_out, and_6_out, and_7_out);

  // Notes on the sheet:
  //   op1
  //   op2
  //   op3
  //   op4
  //   op5
  //   isCall
  //   isB
  //   isBeq
  //   isBgt
  //   isNop
  //   isNot
  //   isMov
endmodule

module _6_B_belongsTo (
  input  [4:0] opcode,
  output out_2
);

  wire and_1_out, and_2_out, and_3_out, and_4_out, and_5_out, and_6_out, and_7_out;

  and and_1 (and_1_out, opcode[0], opcode[1], opcode[2], opcode[3], ~opcode[4]);  // AND_Gate
  and and_2 (and_2_out, ~opcode[0], opcode[1], ~opcode[2], ~opcode[3], opcode[4]);  // AND_Gate
  and and_3 (and_3_out, ~opcode[0], ~opcode[1], ~opcode[2], ~opcode[3], opcode[4]);  // AND_Gate
  and and_4 (and_4_out, opcode[0], ~opcode[1], ~opcode[2], ~opcode[3], opcode[4]);  // AND_Gate
  and and_5 (and_5_out, ~opcode[0], ~opcode[1], opcode[2], ~opcode[3], opcode[4]);  // AND_Gate
  and and_6 (and_6_out, opcode[0], ~opcode[1], opcode[2], ~opcode[3], ~opcode[4]);  // AND_Gate
  and and_7 (and_7_out, opcode[0], ~opcode[1], opcode[2], ~opcode[4]);  // AND_Gate
  or or_1 (out_2, and_1_out, and_2_out, and_3_out, and_4_out, and_5_out, and_6_out, and_7_out);

  // Notes on the sheet:
  //   op1
  //   op2
  //   op3
  //   op4
  //   op5
  //   isSt
  //   isB
  //   isBeq
  //   isBgt
  //   isNop
  //   isRet
  //   cmp
endmodule

module _7_A_belongsTo (
  input  [4:0] opcode,
  output out_2
);

  wire and_1_out, and_2_out, and_3_out, and_4_out, and_5_out, not_1_out, not_2_out, not_3_out, not_4_out;

  not not_1 (not_1_out, opcode[1]);
  not not_2 (not_2_out, opcode[0]);
  not not_3 (not_3_out, opcode[1]);
  not not_4 (not_4_out, opcode[2]);
  and and_1 (and_1_out, opcode[0], not_1_out, opcode[2], opcode[3], ~opcode[4]);  // AND_Gate
  and and_2 (and_2_out, ~opcode[0], opcode[1], ~opcode[2], ~opcode[3], opcode[4]);  // AND_Gate
  and and_3 (and_3_out, ~opcode[0], ~opcode[1], ~opcode[2], ~opcode[3], opcode[4]);  // AND_Gate
  and and_4 (and_4_out, opcode[0], ~opcode[1], ~opcode[2], ~opcode[3], opcode[4]);  // AND_Gate
  and and_5 (and_5_out, ~not_2_out, ~not_3_out, not_4_out, ~opcode[3], opcode[4]);  // AND_Gate
  or or_1 (out_2, and_1_out, and_2_out, and_3_out, and_4_out, and_5_out);

  // Notes on the sheet:
  //   op1
  //   op2
  //   op3
  //   op4
  //   op5
  //   isNop
  //   Is Branch
  //   isBeq
  //   isBgt
  //   isCall
endmodule

module _7_B_belongsTo (
  input  [4:0] opcode,
  output out_2
);

  wire and_1_out, and_2_out, and_3_out, and_4_out, and_5_out, and_6_out, and_7_out;

  and and_1 (and_1_out, opcode[0], opcode[1], opcode[2], opcode[3], ~opcode[4]);  // AND_Gate
  and and_2 (and_2_out, ~opcode[0], opcode[1], ~opcode[2], ~opcode[3], opcode[4]);  // AND_Gate
  and and_3 (and_3_out, ~opcode[0], ~opcode[1], ~opcode[2], ~opcode[3], opcode[4]);  // AND_Gate
  and and_4 (and_4_out, opcode[0], ~opcode[1], ~opcode[2], ~opcode[3], opcode[4]);  // AND_Gate
  and and_5 (and_5_out, ~opcode[0], ~opcode[1], opcode[2], ~opcode[3], opcode[4]);  // AND_Gate
  and and_6 (and_6_out, opcode[0], ~opcode[1], opcode[2], ~opcode[3], ~opcode[4]);  // AND_Gate
  and and_7 (and_7_out, opcode[0], ~opcode[1], opcode[2], ~opcode[4]);  // AND_Gate
  or or_1 (out_2, and_1_out, and_2_out, and_3_out, and_4_out, and_5_out, and_6_out, and_7_out);

  // Notes on the sheet:
  //   op1
  //   op2
  //   op3
  //   op4
  //   op5
  //   isSt
  //   isB
  //   isBeq
  //   isBgt
  //   isNop
  //   isRet
  //   cmp
endmodule

module RS1_Conflict (
  input  [31:0] in_1,
  input  [31:0] in_2,
  output out_3
);

  wire and_1_out, and_2_out, comparator_1_eq, n6_a_belongsto_1_out_2, n6_b_belongsto_1_out_2, not_1_out,
       not_2_out, or_1_out;
  wire [3:0] multiplexer_1_out, multiplexer_2_out;

  _6_A_belongsTo u_6_a_belongsto_1 (.opcode(in_1[31:27]), .out_2(n6_a_belongsto_1_out_2));
  _6_B_belongsTo u_6_b_belongsto_1 (.opcode(in_2[31:27]), .out_2(n6_b_belongsto_1_out_2));
  and and_1 (and_1_out, ~in_1[27], ~in_1[28], in_1[29], ~in_1[30], in_1[31]);  // AND_Gate
  Multiplexer #(.width(4), .enable("false")) multiplexer_1 (
    .in0(in_1[21:18]), .in1(4'b1111), .out(multiplexer_1_out), .sel(and_1_out));
  Multiplexer #(.width(4), .enable("false")) multiplexer_2 (
    .in0(in_2[25:22]), .in1(4'b1111), .out(multiplexer_2_out), .sel(and_2_out));
  and and_2 (and_2_out, in_2[27], in_2[28], ~in_2[29], ~in_2[30], in_2[31]);  // AND_Gate
  not not_1 (not_1_out, comparator_1_eq);
  Comparator #(.width(4)) comparator_1 (
    .a(multiplexer_1_out), .b(multiplexer_2_out), .eq(comparator_1_eq));  // open: gt, lt
  not not_2 (not_2_out, 1'b1);
  or or_1 (or_1_out, n6_a_belongsto_1_out_2, not_1_out, n6_b_belongsto_1_out_2);
  Multiplexer #(.enable("false")) multiplexer_3 (.in0(1'b1), .in1(not_2_out), .out(out_3), .sel(or_1_out));

  // Notes on the sheet:
  //   A
  //   B
  //   A.rs1
  //   A.rs2
  //   A.opcode
  //   B.rs1
  //   B.rs2
  //   B.opcode
  //   A.rd
  //   6_A.belongsTo
  //   ra=r15
  //   B.rd
  //   6_B.belongsTo
  //   isRet
  //   isCall
  //   src1
  //   dest
endmodule

module RS2_Conflict (
  input  [31:0] in_1,
  input  [31:0] in_2,
  output out_3
);

  wire and_1_out, and_2_out, and_3_out, comparator_1_eq, n7_a_belongsto_1_out_2, n7_b_belongsto_1_out_2,
       not_1_out, not_2_out, not_3_out, or_1_out;
  wire [3:0] multiplexer_1_out, multiplexer_2_out;

  _7_A_belongsTo u_7_a_belongsto_1 (.opcode(in_1[31:27]), .out_2(n7_a_belongsto_1_out_2));
  _7_B_belongsTo u_7_b_belongsto_1 (.opcode(in_2[31:27]), .out_2(n7_b_belongsto_1_out_2));
  not not_1 (not_1_out, and_1_out);
  and and_1 (and_1_out, in_1[27], in_1[28], in_1[29], in_1[30], ~in_1[31]);  // AND_Gate
  and and_2 (and_2_out, in_2[27], in_2[28], ~in_2[29], ~in_2[30], in_2[31]);  // AND_Gate
  and and_3 (and_3_out, in_1[26], not_1_out);
  Multiplexer #(.width(4), .enable("false")) multiplexer_1 (
    .in0(in_1[17:14]), .in1(in_1[25:22]), .out(multiplexer_1_out), .sel(and_1_out));
  Multiplexer #(.width(4), .enable("false")) multiplexer_2 (
    .in0(in_2[25:22]), .in1(4'b1111), .out(multiplexer_2_out), .sel(and_2_out));
  Comparator #(.width(4)) comparator_1 (
    .a(multiplexer_1_out), .b(multiplexer_2_out), .eq(comparator_1_eq));  // open: gt, lt
  not not_2 (not_2_out, 1'b1);
  or or_1 (or_1_out, n7_a_belongsto_1_out_2, and_3_out, not_3_out, n7_b_belongsto_1_out_2);
  not not_3 (not_3_out, comparator_1_eq);
  Multiplexer #(.enable("false")) multiplexer_3 (.in0(1'b1), .in1(not_2_out), .out(out_3), .sel(or_1_out));

  // Notes on the sheet:
  //   A
  //   B
  //   A.rs1
  //   A.rs2
  //   A.opcode
  //   B.rs1
  //   B.rs2
  //   B.opcode
  //   A.rd
  //   ra=r15
  //   B.rd
  //   ret2
  //   ret1
  //   isCalll
  //   ret3
  //   src2
  //   dest
  //   ret5
  //   ret4
endmodule

module Forwarding_Unit (
  input  [31:0] in_1,
  input  [31:0] in_2,
  input  [31:0] in_3,
  input  [31:0] in_4,
  output M1,
  output M2,
  output [1:0] M3_rw,
  output [1:0] M4_ma,
  output out_9,
  output M6
);

  RS1_Conflict rs1_conflict_1 (.in_1(in_1), .in_2(in_4), .out_3(M1));
  RS2_Conflict rs2_conflict_1 (.in_1(in_1), .in_2(in_4), .out_3(M2));
  RS1_Conflict rs1_conflict_2 (.in_1(in_2), .in_2(in_4), .out_3(M3_rw[0]));
  RS2_Conflict rs2_conflict_2 (.in_1(in_2), .in_2(in_4), .out_3(M4_ma[0]));
  RS1_Conflict rs1_conflict_3 (.in_1(in_2), .in_2(in_3), .out_3(M3_rw[1]));
  RS2_Conflict rs2_conflict_3 (.in_1(in_2), .in_2(in_3), .out_3(M4_ma[1]));
  RS2_Conflict rs2_conflict_4 (.in_1(in_3), .in_2(in_4), .out_3(M6));

  assign out_9 = M4_ma[0];

  // Notes on the sheet:
  //   OF Instruction
  //   EX Instruction
  //   MA  Instruction
  //   RW Instruction
  //   RW-OF
  //   RW-EX
  //   MA-EX
  //   RW-MA
  //   M45_rw
  //   M3_ma
endmodule
